# Fritzing sketch hc-sr501_motion_sensor (saved by Fritzing 0.9.4)

parts:
  부품1 = Arduino Uno (Rev3)
  부품2 = HC-SR501 Body Sensor Module

nets:
  N1: 부품1.D2, 부품2.OUT
  5V: 부품1.5V, 부품2.VCC
  GND: 부품1.GND, 부품2.GND

custom parts:
  HC-SR501 Body Sensor Module: Pyroelectric Infrared PIR Motion Sensor Detector Module

// code stored in the sketch: hc-sr501_motion_sensor.ino
/*
 * Created by ArduinoGetStarted.com
 *
 * This example code is in the public domain
 *
 * Tutorial page: https://arduinogetstarted.com/tutorials/arduino-motion-sensor
 */

const int PIN_TO_SENSOR = 2;   // the pin that OUTPUT pin of sensor is connected to
int pinStateCurrent   = LOW; // current state of pin
int pinStatePrevious  = LOW; // previous state of pin

void setup() {
  Serial.begin(9600);            // initialize serial
  pinMode(PIN_TO_SENSOR, INPUT); // set arduino pin to input mode to read value from OUTPUT pin of sensor
}

void loop() {
  pinStatePrevious = pinStateCurrent; // store old state
  pinStateCurrent = digitalRead(PIN_TO_SENSOR);   // read new state

  if (pinStatePrevious == LOW && pinStateCurrent == HIGH) {   // pin state change: LOW -> HIGH
    Serial.println("Motion detected!");
    // TODO: turn on alarm, light or activate a device ... here
  }
  else
  if (pinStatePrevious == HIGH && pinStateCurrent == LOW) {   // pin state change: HIGH -> LOW
    Serial.println("Motion stopped!");
    // TODO: turn off alarm, light or deactivate a device ... here
  }
}
