# Fritzing sketch sound_sensor (saved by Fritzing 0.9.4)
breadboards: 1

parts:
  부품1 = Breakout Board for Electret Microphone
  부품2 = Arduino Uno (Rev3) - ICSP
  LED1 = LED - 5mm [color="Red (633nm)" package="5 mm [THT]"]
  R1 = Resistor [tolerance=±5% resistance=1k package="2010 [SMD]"]

nets:
  VCC: 부품1.VCC, 부품2.5V
  GND: 부품1.GND, 부품2.GND, LED1.cathode
  N1: 부품1.AUD, 부품2.D2
  N2: LED1.anode, R1.Pin_1

// code stored in the sketch: sound_sensor.ino
int soundSensor=2;
int LED=4;
boolean LEDStatus=false;

void setup() {
 pinMode(soundSensor,INPUT);
 pinMode(LED,OUTPUT);

}

void loop() {

  int SensorData=digitalRead(soundSensor); 
  if(SensorData==1){

    if(LEDStatus==false){
        LEDStatus=true;
        digitalWrite(LED,HIGH);
    }
    else{
        LEDStatus=false;
        digitalWrite(LED,LOW);
    }
  }
 }
