# Fritzing sketch touch_sensor (saved by Fritzing 0.9.4)

parts:
  TTP223B1 = TTP223B Capacitive Touch Sensor Module
  부품1 = Arduino Uno (Rev3)

nets:
  GND: TTP223B1.GND, 부품1.GND
  VCC: TTP223B1.VCC, 부품1.5V
  N1: TTP223B1.SIG, 부품1.D7

custom parts:
  TTP223B Capacitive Touch Sensor Module: The TTP223B capacitive touch sensor module uses the TTP223B IC. The appropriate voltage is approximately 2 to 5.5 volts.

// code stored in the sketch: touch_sensor.ino
// constants won't change. They're used here to set pin numbers:
const int SENSOR_PIN = 7; // the Arduino's input pin that connects to the sensor's SIGNAL pin 

void setup() {
 // initialize serial communication at 9600 bits per second:
 Serial.begin(9600);
 // initialize the Arduino's pin as aninput
 pinMode(SENSOR_PIN, INPUT);
}

void loop() {
 // read the state of the the input pin:
 int state = digitalRead(SENSOR_PIN);

 // print state to Serial Monitor
 Serial.println(state);
}
